# Fritzing sketch thermostat (saved by Fritzing 1.0.4)

parts:
  M1 = 1 chan 5v relay module
  SHT-40 = Adafruit SHT4x [part_number="Adafruit #4885"]
  LCD1 = TFT 3.5 inch 480x320 w touch and SD
  A1 = ESP32-C6-DevKitC-1

nets:
  N1: M1.pin_1, A1.Pin_14
  N2: M1.pin_3, A1.Pin_19
  N3: SHT-40.GND, A1.Pin_15, A1.Pin_32
  N4: SHT-40.SCL, A1.Pin_6
  N5: SHT-40.SDA, A1.Pin_5
  N6: LCD1.Pin_1, A1.Pin_1
  N7: LCD1.Pin_3, A1.Pin_7
  N8: LCD1.Pin_4, A1.Pin_3
  N9: LCD1.Pin_5, A1.Pin_13
  N10: LCD1.Pin_6, A1.Pin_10
  N11: LCD1.Pin_7, A1.Pin_12
  N12: LCD1.Pin_8, A1.Pin_4
  N13: LCD1.Pin_9, A1.Pin_8
  N14: LCD1.Pin_11, A1.Pin_11

notes:
  Connect to the boiler

custom parts:
  1 chan 5v relay module: 1 Channel 5V Relay Module Board Shield with Optocoupler Support High and Low Level Trigger for Arduino.
  Adafruit SHT4x: Sensirion Temperature/Humidity sensors are some of the finest & highest-accuracy devices you can get. And finally, we have some that have a true I2C interface for easy reading. The SHT40 and SHT45 sensors are the fourth generation (started at the SHT10 and worked its way up to the top!). The SHT40 has an excellent ±1.8% typical relative humidity accuracy from 25 to 75% and ±0.2 °C typical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
  TFT 3.5 inch 480x320 w touch and SD: This is a generic 1.8 tft spi lcd display available on ebay and others. The 1.8"3.5 inch 480X320 SPI TFT Module 320x480 LCD Display - Touch.
  ESP32-C6-DevKitC-1: ESP32-C6-DevKitC-1 is an entry-level development board based on ESP32-C6-WROOM-1(U), a general-purpose module with a 8 MB SPI flash. This board integrates complete Wi-Fi, Bluetooth LE, Zigbee, and Thread functions.
